# Fritzing sketch TrafficLight (saved by Fritzing 0.7.12b)
breadboards: 1

parts:
  R3_470_Ohm = Resistor [tolerance=±5% resistance=470 package=THT]
  LED_Red = LED - 5mm [color="Red (633nm)" package="5 mm [THT]"]
  LED_Yellow = LED - 5mm [color="Yellow (595nm)" package="5 mm [THT]"]
  R2_470_Ohm = Resistor [tolerance=±5% resistance=470 package=THT]
  LED_Green = LED - 5mm [color="Green (570nm)" package="5 mm [THT]"]
  R1_470_Ohm = Resistor [tolerance=±5% resistance=470 package=THT]
  Stromquelle_12_V = Battery
  K1 = Relay [part_number=FRS1B-S package=THT]
  Relay_2 = Relay [part_number=FRS1B-S package=THT]

nets:
  N1: R3_470_Ohm.Pin_0, R2_470_Ohm.Pin_0, R1_470_Ohm.Pin_0, Stromquelle_12_V.-
  N2: R3_470_Ohm.Pin_1, LED_Green.cathode
  N3: LED_Red.cathode, R1_470_Ohm.Pin_1
  N4: LED_Red.anode, K1.B
  N5: LED_Yellow.cathode, R2_470_Ohm.Pin_1
  N6: LED_Yellow.anode, K1.A
  N7: LED_Green.anode, Relay_2.A
  N8: Stromquelle_12_V.+, Relay_2.C1, Relay_2.C2
  N9: K1.C1, Relay_2.B

notes:
  A1
  SW1
  B1
  A2
  B2
  SW2
  Relay 2
  Relay 1
